# Fritzing sketch RoboticArm_Circuit_Diagram (saved by Fritzing 1.0.2b)
breadboards: 1

parts:
  Componente1 = Arduino Mega ADK (Rev3)
  Componente2 = 16-Channel 12-bit PWM Servo Driver - I2C [part_number=815]
  BAT1 = BC9VPC [package=bc9vpc]
  M1 = RioRand LM2596
  Mojo1 = Embedded Micro Mojo v3
  BAT2 = BC9VPC [package=bc9vpc]
  M2 = RioRand LM2596
  BAT3 = BC9VPC [package=bc9vpc]
  M3 = RioRand LM2596
  J9 = Basic Servo
  J10 = Basic Servo
  J11 = Basic Servo
  J12 = Basic Servo

nets:
  N1: Componente1.D21/SCL, Mojo1.119
  N2: Componente1.D20/SDA, Mojo1.118
  VCC: Componente1.5V, Componente2.5.0V, M2.Pin_3, J9.vcc, J10.vcc, J11.vcc, J12.vcc
  GND: Componente1.GND, Componente2.GND, M2.Pin_4, M3.Pin_4, J9.gnd, J10.gnd, J11.gnd, J12.gnd
  N3: Componente2.PWRIN, M3.Pin_3
  N4: Componente2.PWM3, J11.pulse
  N5: Componente2.PWM2, J10.pulse
  N6: Componente2.PWM1, J9.pulse
  N7: Componente2.PWM0, J12.pulse
  N8: BAT1.V+, M1.Pin_1
  N9: BAT1.V-, M1.Pin_2
  N10: BAT2.V+, M2.Pin_1
  N11: BAT2.V-, M2.Pin_2
  N12: BAT3.V+, M3.Pin_1
  N13: BAT3.V-, M3.Pin_2

custom parts:
  16-Channel 12-bit PWM Servo Driver - I2C: You want to make a cool robot, maybe a hexapod walker, or maybe just a piece of art with a lot of moving parts. Or maybe you want to drive a lot of LEDs with precise PWM output. Using only two pins, control 16 free-running PWM outputs! You can even chain up 62 breakouts to control up to 992 PWM outputs.
  Embedded Micro Mojo v3: The Mojo is a FPGA development board that is designed from the ground up to be easy to use. The entire goal of the Mojo is to make getting started with FPGA and digital design as easy as possible. To go along with our board, Embedded Micro has tutorials to help you get started and expand your knowledge of digital design. The Mojo is made in the USA. The Mojo features include: Spartan 6 XC6SLX9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
